# Fritzing sketch Servo_ver (saved by Fritzing 1.0.5)
breadboards: 1

parts:
  Part1 = Arduino Uno (Rev3)
  Mod1 = Raspberry Pi 4B
  LLC1 = Logic Level Converter [package="Breakout board"]
  M1 = Dagu DGServo 9g (Top view) [part_number=RS001B]
  IC1 = Rasberry Pi NIOR Camera [chip_label=IC package="DIP (Dual Inline) [THT]"]  # not connected
  M2 = Dagu DGServo 9g (Top view) [part_number=RS001B]

nets:
  GND: Part1.GND, LLC1.H-GND, M1.gnd
  N1: Part1.D0/RX, LLC1.HV3
  N2: Part1.D1/TX, LLC1.HV4
  N3: Part1.D3_PWM, M2.pulse
  N4: Part1.D4, M1.pulse
  VCC: Part1.5V, LLC1.HV, M1.vcc, M2.vcc
  N5: Mod1.3V3, LLC1.LV
  N6: Mod1.GND, LLC1.L-GND
  N7: Mod1.GPIO14, LLC1.LV4
  N8: Mod1.GPIO15, LLC1.LV3

custom parts:
  Logic Level Converter: 5V to/from 3.3V logic level converter
  Rasberry Pi NIOR Camera: Camera
